// Logisim project CPU_8_BITS.circ as structural Verilog
module DATAPATH (
  input  [7:0] Memory_Data,
  input  PC_REG,
  input  Clear,
  input  ULA3,
  input  ULA2,
  input  ULA1,
  input  ULA0,
  input  OUT_REG,
  input  MBR_REG,
  input  B_REG,
  input  A_REG,
  input  Clock,
  input  SELECT_BUS1,
  input  SELECT_BUS0,
  input  [7:0] Input_Exter,
  output [7:0] Memory_Addr,
  output [7:0] OUT
);

  wire [7:0] A_q, B_q, MBR_q, multiplexer_1_out, ula_1_s;

  Register A (.D(ula_1_s), .en(A_REG), .Q(A_q), .clk(Clock), .clr(Clear));
  Register B (.D(ula_1_s), .en(B_REG), .Q(B_q), .clk(Clock), .clr(Clear));
  Register MBR (.D(Memory_Data), .en(MBR_REG), .Q(MBR_q), .clk(Clock), .clr(Clear));
  Register PC (.D(ula_1_s), .en(PC_REG), .Q(Memory_Addr), .clk(Clock), .clr(Clear));
  Register u_OUT (.D(ula_1_s), .en(OUT_REG), .Q(OUT), .clk(Clock), .clr(Clear));
  Multiplexer #(.select(2), .width(8)) multiplexer_1 (
    .in0(B_q), .in1(MBR_q), .in2(Memory_Addr), .in3(Input_Exter), .out(multiplexer_1_out),
    .sel({SELECT_BUS1, SELECT_BUS0}), .en(1'b1));
  ULA ula_1 (.A(A_q), .B(multiplexer_1_out), .in_3({ULA3, ULA2, ULA1, ULA0}), .S(ula_1_s));

  // Notes on the sheet:
  //   00000 - A
  //   00001 - B
  //   00010 - A + 1
  //   00011 - B + 1
  //   00100 - and
  //   00101 - or
  //   00110 - nand
  //   00111 - xor
  //   01000 - soma de naturais
  //   01001 - soma de inteiros
  //   01010 - subtração
endmodule

module UNIDADE_DE_CONTROLE (
  input  CLK,
  input  Clear,
  output [7:0] OUT
);

  wire [4:0] bit_extender_1_out, MIR_q_3, MPC_q, multiplexer_1_out;
  wire [7:0] Memory_Addr, Memory_Data, MIR_q;
  wire [19:8] MIR_q_2;
  wire [24:0] rom_1_data;

  Bit_Extender #(.out_width(5)) bit_extender_1 (.in(OUT), .out(bit_extender_1_out));
  DATAPATH datapath_1 (
    .Clock(CLK), .Memory_Data(Memory_Data), .OUT_REG(MIR_q_2[12]), .PC_REG(MIR_q_2[11]),
    .MBR_REG(MIR_q_2[10]), .B_REG(MIR_q_2[9]), .A_REG(MIR_q_2[8]), .Clear(Clear), .ULA3(MIR_q_2[18]),
    .ULA2(MIR_q_2[17]), .ULA1(MIR_q_2[16]), .ULA0(MIR_q_2[15]), .Input_Exter(MIR_q),
    .SELECT_BUS1(MIR_q_2[14]), .SELECT_BUS0(MIR_q_2[13]), .Memory_Addr(Memory_Addr), .OUT(OUT));
  Multiplexer #(.width(5)) multiplexer_1 (
    .in0(MIR_q_3), .in1(bit_extender_1_out), .out(multiplexer_1_out), .sel(MIR_q_2[19]));  // open: en
  Register #(.width(5)) MPC (.D(multiplexer_1_out), .Q(MPC_q), .clk(CLK), .clr(Clear));  // open: en
  ROM #(.addrWidth(5), .dataWidth(25)) rom_1 (.addr(MPC_q), .data(rom_1_data));  // open: sel
  Register #(.width(25)) MIR (.D(rom_1_data), .Q({MIR_q_3, MIR_q_2, MIR_q}), .clk(CLK), .clr(Clear));  // open: en
  RAM #(.bus("asynch")) ram_1 (.addr(Memory_Addr), .data(Memory_Data), .sel(1'b1), .ld(1'b1));  // open: clr

  // Notes on the sheet:
  //   contents of rom_1 (hex, n*v repeats v):
  //   10e10a 201000 30e208 409000 521000
endmodule
