// Logisim project ULA.circ as structural Verilog: 1 circuit, main circuit ULA
module ULA (
  input  [7:0] A,
  input  [7:0] B,
  input  [3:0] in_3,
  output [7:0] S
);

  wire [7:0] adder_1_out, adder_2_out, adder_3_out, and_1_out, nand_1_out, or_1_out, subtractor_1_out,
       xor_1_out;

  assign and_1_out = A & B;  // AND_Gate and_1, 8 bits wide
  assign or_1_out = A | B;  // OR_Gate or_1, 8 bits wide
  assign nand_1_out = ~(A & B);  // NAND_Gate nand_1, 8 bits wide
  assign xor_1_out = A ^ B;  // XOR_Gate xor_1, 8 bits wide
  Adder adder_1 (.a(A), .b(B), .out(adder_1_out));  // open: cin, cout
  Subtractor subtractor_1 (.a(A), .b(B), .out(subtractor_1_out));  // open: bin, bout
  Adder adder_2 (.a(A), .b(8'h1), .out(adder_2_out));  // open: cin, cout
  Adder adder_3 (.a(B), .b(8'h1), .out(adder_3_out));  // open: cin, cout
  Multiplexer #(.select(4), .width(8), .enable("false")) multiplexer_1 (
    .in0(A), .in1(B), .in2(adder_2_out), .in3(adder_3_out), .in4(and_1_out), .in5(or_1_out),
    .in6(nand_1_out), .in7(xor_1_out), .in8(adder_1_out), .in9(adder_1_out), .in10(subtractor_1_out),
    .out(S), .sel(in_3));  // open: in11, in12, in13, in14, in15

  // Notes on the sheet:
  //   00000 - A
  //   00001 - B
  //   00010 - A + 1
  //   00011 - B + 1
  //   00100 - and
  //   00101 - or
  //   00110 - nand
  //   00111 - xor
  //   01000 - soma de naturais
  //   01001 - soma de inteiros
  //   01010 - subtração
endmodule
